# Fritzing sketch Gymproto(PROMINI) (saved by Fritzing 0.9.3b)

parts:
  SEN1 = Pulse Sensor [package=SIP]
  BATT1 = LiPoly Battery (1300mAh)
  부품2 = Bluetooth HC-05 Macho
  o1 = Module display OLED I2C 128x64 SSD1306 [package=THT]
  부품1 = Arduino Pro Mini v13
  부품3 = FTDI Basic Programmer
  TP1 = TP4056 [chip_label=TP4056 package="DIP (Dual Inline) [THT]"]

nets:
  VCC: SEN1.Vcc, 부품1.VCC
  GND: SEN1.GND, 부품1.GND, TP1.pin6
  N1: BATT1.positive, TP1.pin4
  N2: BATT1.negative, TP1.pin5
  N3: 부품2.TXD, 부품1.D2
  N4: 부품2.RXD, 부품1.D3_PWM
  N5: o1.SCL, 부품1.A5
  N6: o1.SDA, 부품1.A4
  N7: 부품1.D0/TX, 부품3.TXO
  N8: 부품1.D1/RX, 부품3.RXI
  N9: 부품1.RAW, TP1.pin3

custom parts:
  Pulse Sensor: Pulse Sensor Optical Heart Rate Monitor for Arduino and other microcontrollers
  LiPoly Battery (1300mAh): Lithium Ion Polymer Battery (1300mAh)
  Module display OLED I2C 128x64 SSD1306: Ecran OLED I2C SSD163 de 128x64 avec connexion I2C
  TP4056: A DIP stand-in part for whatever IC you want. With 6 pins on a 300mil dual inline package (DIP) footprint.
