# Fritzing sketch Gymproto1 (saved by Fritzing 0.9.3b)

parts:
  부품3 = Bluetooth HC-05 Macho
  o1 = Module display OLED I2C 128x64 SSD1306 [package=THT]
  부품2 = Arduino Uno (Rev3)
  M1 = MAX30102

nets:
  N1: 부품3.TXD, 부품2.D2
  N2: 부품3.RXD, 부품2.D3_PWM
  GND: o1.GND, 부품2.GND, M1.GND
  VCC: o1.VCC, 부품2.5V, M1.VIN
  N3: o1.SCL, 부품2.A5/SCL, M1.SCL
  N4: o1.SDA, 부품2.A4/SDA, M1.SDA

custom parts:
  Module display OLED I2C 128x64 SSD1306: Ecran OLED I2C SSD163 de 128x64 avec connexion I2C
  MAX30102: Oximeter module using the MAX30102 chip. You may wish to read (and check your module) this post on power problems with these modules: https://reedpaper.wordpress.com/2018/08/22/pulse-oximeter-max30100-max30102-how-to-fix-wrong-board/ . As usual, if you want the mounting holes in pcb, you need to drag a hole over the pad in silkscreen to actually drill the hole (by default they are not drilled)
